# Fritzing sketch ArduinoUno.DHT22.HC-42 (saved by Fritzing 0.9.3b)
breadboards: 1

parts:
  Part2 = Bluetooth HC-42 Macho
  DHT1 = DHT22 Humidity and Temperature Sensor
  Part3 = Arduino Uno (Rev3)

nets:
  N1: Part2.TXD, Part3.D0/RX
  N2: Part2.RXD, Part3.D1/TX
  VCC: Part2.VCC, DHT1.VDD, Part3.3V3
  GND: Part2.GND, DHT1.GND, Part3.GND
  N3: DHT1.DATA, Part3.D8

custom parts:
  Bluetooth HC-42 Macho: HC-42, supporting BLE 5.0
